// Logisim project Master_Slave_J-K_Flipflop.circ as structural Verilog: 1 circuit, main circuit main
module main (
  input  J,
  input  K,
  output out_3,
  output out_4
);

  wire clock_1_out, n7400_1_p3, n7400_2_p3, n7400_3_p3, n7410_1_p6, n7410_1_p8, n7410_1_p10, n7410_2_p6;

  Clock clock_1 (.out(clock_1_out));
  // _7410 7410_1: pin names not known; wires that end beside it: clock_1_out, J, 1'b0, 1'b1, out_4, n7410_1_p6, n7410_1_p6, n7410_1_p8, n7410_1_p8, n7410_1_p10
  // _7410 7410_2: pin names not known; wires that end beside it: clock_1_out, K, 1'b0, 1'b1, out_3, n7410_2_p6, n7410_2_p6, n7410_1_p10, n7410_1_p10, n7410_1_p8
  // _7400 7400_1: pin names not known; wires that end beside it: clock_1_out, clock_1_out, n7400_1_p3, 1'b0, 1'b1
  // _7400 7400_2: pin names not known; wires that end beside it: n7400_1_p3, n7410_1_p10, n7400_2_p3, 1'b0, 1'b1, n7400_2_p3, out_4, out_3
  // _7400 7400_3: pin names not known; wires that end beside it: n7400_1_p3, n7410_1_p8, n7400_3_p3, 1'b0, 1'b1, n7400_3_p3, out_3, out_4

  // Notes on the sheet:
  //   1905105
endmodule
