// Logisim project Universal_Shift_Register.circ as structural Verilog: 1 circuit, main circuit main
module main (
  input  I3,
  input  I2,
  input  I1,
  input  I0,
  input  Shift_Right_Input,
  input  Shift_Left_Input,
  input  S1,
  input  S0,
  input  CLEAR,
  output A3,
  output A2,
  output A1,
  output A0
);

  wire CLK_out, n74153_1_p7, n74153_1_p16, n74153_2_p7, n74153_2_p16;

  Clock CLK (.out(CLK_out));
  // _74153 74153_1: pin names not known; wires that end beside it: 1'b0, S1, I3, A2, Shift_Right_Input, A3, n74153_1_p7, 1'b0, 1'b1, 1'b0, S0, I2, A1, A3, A2, n74153_1_p16
  // _7474 7474_1: pin names not known; wires that end beside it: CLEAR, n74153_1_p7, CLK_out, A3, 1'b0, 1'b1, CLEAR, n74153_1_p16, CLK_out, A2
  // _74153 74153_2: pin names not known; wires that end beside it: 1'b0, S1, I1, A0, A2, A1, n74153_2_p7, 1'b0, 1'b1, 1'b0, S0, I0, Shift_Left_Input, A1, A0, n74153_2_p16
  // _7474 7474_2: pin names not known; wires that end beside it: CLEAR, n74153_2_p7, CLK_out, A1, 1'b0, 1'b1, CLEAR, n74153_2_p16, CLK_out, A0

  // Notes on the sheet:
  //   1905105
endmodule
