// Logisim project 1905105.circ as structural Verilog: 2 circuits, main circuit main
module main (
  input  Xo,
  input  X1,
  input  X2,
  input  X3,
  output F_X,
  output F_X__prime
);

  wire n7404_1_p2, n7404_1_p4, n7404_1_p6, n7408_1_p3, n7408_1_p6, n7408_1_p8, n7408_2_p3, n7408_2_p6,
       n7408_2_p10, n7408_2_p11;

  // _7404 7404_1: pin names not known; wires that end beside it: Xo, n7404_1_p2, X2, n7404_1_p4, X3, n7404_1_p6, 1'b0, 1'b1, F_X, F_X__prime
  // _7408 7408_1: pin names not known; wires that end beside it: Xo, X1, n7408_1_p3, 1'b0, 1'b1, n7408_1_p6, n7408_1_p3, n7408_1_p8
  // _7408 7408_2: pin names not known; wires that end beside it: n7404_1_p6, Xo, n7408_2_p3, X1, n7404_1_p2, n7408_2_p6, 1'b0, 1'b1, X2, n7408_2_p10, n7408_2_p11
  // _7432 7432_1: pin names not known; wires that end beside it: n7408_2_p6, n7408_2_p3, n7408_2_p10, n7404_1_p4, n7404_1_p6, n7408_1_p6, 1'b0, 1'b1, n7408_2_p11, n7408_1_p8, F_X
endmodule

module F_A__F_B__F_A_F_B (
  input  [3:0] B,
  input  [3:0] A,
  output out_3
);

  wire n7408_1_p1, n7408_1_p2, n7408_1_p3, n7408_1_p6, n7408_1_p7, n7408_1_p8;

  // _7408 7408_1: pin names not known; wires that end beside it: n7408_1_p1, n7408_1_p2, n7408_1_p3, 1'b0, 1'b1, n7408_1_p6, n7408_1_p7, n7408_1_p8
  main main_1 (.Xo(A[3]), .X1(A[2]), .X2(A[1]), .X3(A[0]), .F_X(n7408_1_p1), .F_X__prime(n7408_1_p6));
  main main_2 (.Xo(B[3]), .X1(B[2]), .X2(B[1]), .X3(B[0]), .F_X(n7408_1_p7), .F_X__prime(n7408_1_p2));
  // _7432 7432_1: pin names not known; wires that end beside it: n7408_1_p8, n7408_1_p3, out_3, 1'b0, 1'b1
endmodule
