// Logisim project 1905105.circ as structural Verilog: 1 circuit, main circuit main
module main (
  input  W,
  input  X,
  input  Y,
  input  Z,
  output F
);

  wire n7404_1_p5, n7408_1_p3, n7408_1_p6, n74138_1_p10, n74138_1_p13, n74138_1_p14, n74138_1_p15,
       n74138_2_p7;

  // _74138 74138_1: pin names not known; wires that end beside it: Z, Y, X, W, Z, Y, X, 1'b0, 1'b0, n74138_1_p10, 1'b0, 1'b1, n74138_1_p13, n74138_1_p14, n74138_1_p15
  // _7404 7404_1: pin names not known; wires that end beside it: W, n74138_1_p10, 1'b0, 1'b1, n7404_1_p5, F
  // _74138 74138_2: pin names not known; wires that end beside it: Z, Y, X, 1'b0, 1'b0, W, n74138_2_p7, 1'b0, 1'b1
  // _7408 7408_1: pin names not known; wires that end beside it: n74138_1_p13, n74138_1_p14, n7408_1_p3, n7408_1_p3, n74138_1_p15, n7408_1_p6, 1'b0, 1'b1, n7408_1_p6, n74138_2_p7, n7404_1_p5
endmodule
