// Logisim project 1905105.circ as structural Verilog: 1 circuit, main circuit main
module main (
  input  A,
  input  B,
  input  C,
  input  D,
  output F
);

  wire n74153_1_p4, n74153_1_p6;

  // _74153 74153_1: pin names not known; wires that end beside it: 1'b0, A, 1'b0, n74153_1_p4, 1'b1, n74153_1_p6, F, 1'b0, 1'b1, B
  // _7404 7404_1: pin names not known; wires that end beside it: n74153_1_p4, n74153_1_p6, 1'b1
  // _7432 7432_1: pin names not known; wires that end beside it: C, D, n74153_1_p4, 1'b0, 1'b1, 1'b0
endmodule
