// Logisim project 1905105.circ as structural Verilog: 1 circuit, main circuit main
module main (
  input  in_1,
  output out_2,
  output out_3,
  output out_4
);

  wire n7408_1_p3, n7408_1_p6, n7408_1_p10, n7408_1_p11, n7408_1_p14, n7476_1_p1, n7476_1_p3, n7476_1_p7,
       n7476_1_p9, n7476_1_p13, n7476_1_p14;

  // _7476 7476_1: pin names not known; wires that end beside it: n7476_1_p1, in_1, n7476_1_p3, 1'b1, n7476_1_p1, in_1, n7476_1_p7, out_2, n7476_1_p9, 1'b0, 1'b1, out_3, n7476_1_p13, n7476_1_p14
  // _7408 7408_1: pin names not known; wires that end beside it: n7476_1_p9, n7476_1_p13, n7408_1_p3, n7476_1_p9, out_3, n7408_1_p6, 1'b0, 1'b1, n7476_1_p13, n7408_1_p10, n7408_1_p11, out_3, out_4, n7408_1_p14
  Clock clock_1 (.out(n7476_1_p1));
  // _7476 7476_2: pin names not known; wires that end beside it: n7476_1_p1, in_1, n7408_1_p3, 1'b1, n7408_1_p6, out_4, n7408_1_p10, 1'b0
  // _7432 7432_1: pin names not known; wires that end beside it: out_3, n7408_1_p10, n7476_1_p7, n7408_1_p11, n7408_1_p14, n7476_1_p3, 1'b0, 1'b1, out_2, out_4, n7476_1_p14

  // Notes on the sheet:
  //   7 - 1 - 3 - 4 - 2 - 0 - 5
endmodule
